// Logisim project IT012_Lab01_25520756.circ as structural Verilog
module TN3 (
  input  A,
  input  B,
  input  C,
  input  D,
  output F
);

  wire and_1_out, and_2_out, and_3_out, and_4_out, and_5_out, and_6_out, not_1_out, not_2_out, not_3_out,
       not_4_out;

  not not_1 (not_1_out, A);
  not not_2 (not_2_out, B);
  not not_3 (not_3_out, C);
  not not_4 (not_4_out, D);
  and and_1 (and_1_out, not_1_out, not_2_out, C, not_4_out);
  and and_2 (and_2_out, not_1_out, not_2_out, C, D);
  and and_3 (and_3_out, not_1_out, B, not_3_out, D);
  and and_4 (and_4_out, not_1_out, B, C, D);
  and and_5 (and_5_out, A, not_2_out, C, D);
  and and_6 (and_6_out, A, B, not_3_out, D);
  or or_1 (F, and_1_out, and_2_out, and_3_out, and_4_out, and_5_out, and_6_out);
endmodule

module TN4 (
  input  A,
  input  B,
  input  C,
  input  D,
  output F_can,
  output F_SoP,
  output F_PoS,
  output EQ1,
  output EQ2
);

  wire and_1_out, and_2_out, and_3_out, and_4_out, and_5_out, and_6_out, and_7_out, and_8_out, and_9_out,
       and_10_out, not_1_out, not_2_out, not_3_out, not_4_out, or_3_out, or_4_out, or_5_out, or_6_out,
       or_7_out;

  not not_1 (not_1_out, A);
  not not_2 (not_2_out, B);
  not not_3 (not_3_out, C);
  not not_4 (not_4_out, D);
  and and_1 (and_1_out, not_1_out, not_2_out, C, not_4_out);
  and and_2 (and_2_out, not_1_out, not_2_out, C, D);
  and and_3 (and_3_out, not_1_out, B, not_3_out, D);
  or or_1 (F_can, and_1_out, and_2_out, and_3_out, and_4_out, and_5_out, and_6_out);
  and and_4 (and_4_out, not_1_out, B, C, D);
  and and_5 (and_5_out, A, not_2_out, C, D);
  xnor xnor_1 (EQ1, F_can, F_SoP);
  and and_6 (and_6_out, A, B, not_3_out, D);
  and and_7 (and_7_out, not_1_out, not_2_out, C);
  and and_8 (and_8_out, not_1_out, B, D);
  and and_9 (and_9_out, B, not_3_out, D);
  or or_2 (F_SoP, and_7_out, and_8_out, and_9_out, and_10_out);
  xnor xnor_2 (EQ2, F_can, F_PoS);
  and and_10 (and_10_out, not_2_out, C, D);
  or or_3 (or_3_out, B, C);
  or or_4 (or_4_out, not_2_out, D);
  or or_5 (or_5_out, C, D);
  and and_11 (F_PoS, or_3_out, or_5_out, or_4_out, or_6_out, or_7_out);
  or or_6 (or_6_out, not_1_out, D);
  or or_7 (or_7_out, not_1_out, not_2_out, not_3_out);
endmodule

module TN5 (
  input  C,
  input  A,
  input  B,
  output F
);

  wire xor_1_out;

  xor xor_1 (xor_1_out, A, B);
  xor xor_2 (F, C, xor_1_out);
endmodule

module TN1 (
  input  A,
  input  B,
  input  C,
  output A_prime,
  output AB,
  output A___B,
  output CHAIN,
  output NAND_A__B,
  output NOR_A__B,
  output XOR_A__B,
  output XNOR_A__B,
  output XOR3,
  output NAND3
);

  not not_1 (A_prime, A);
  and and_1 (AB, A, B);
  or or_1 (A___B, A, B);
  nand nand_1 (NAND_A__B, A, B);
  nor nor_1 (NOR_A__B, A, B);
  xor xor_1 (XOR_A__B, A, B);
  xnor xnor_1 (XNOR_A__B, A, B);
  ExactlyOne xor_2 (.out(XOR3), .in0(A), .in1(B), .in2(C));
  nand nand_2 (NAND3, A, B, C);
  nand nand_3 (CHAIN, C, NAND_A__B);
endmodule

module TN2 (
  input  X,
  input  Y,
  input  Z,
  output EQ1,
  output EQ2,
  output EQ3,
  output EQ4,
  output EQ5
);

  wire and_1_out, and_2_out, and_3_out, and_4_out, and_5_out, and_6_out, nand_1_out, nor_1_out, not_1_out,
       not_2_out, not_3_out, not_4_out, or_1_out, or_2_out, or_3_out, or_4_out, or_5_out, or_6_out;

  not not_1 (not_1_out, X);
  not not_2 (not_2_out, X);
  not not_3 (not_3_out, Y);
  not not_4 (not_4_out, X);
  nor nor_1 (nor_1_out, X, Y);
  and and_1 (and_1_out, not_3_out, not_4_out);
  nand nand_1 (nand_1_out, Y, X);
  and and_2 (and_2_out, not_3_out, not_4_out);
  and and_3 (and_3_out, Y, Z);
  or or_1 (or_1_out, X, Y);
  or or_2 (or_2_out, X, Z);
  and and_4 (and_4_out, not_1_out, Y);
  and and_5 (and_5_out, not_2_out, Y);
  and and_6 (and_6_out, or_1_out, or_2_out);
  or or_3 (or_3_out, and_4_out, X);
  or or_4 (or_4_out, and_5_out, X);
  or or_5 (or_5_out, X, Y);
  or or_6 (or_6_out, and_3_out, X);
  xnor xnor_1 (EQ1, nor_1_out, and_1_out);
  xnor xnor_2 (EQ2, nand_1_out, and_2_out);
  xnor xnor_3 (EQ3, or_6_out, and_6_out);
  xnor xnor_4 (EQ4, or_3_out, X);
  xnor xnor_5 (EQ5, or_4_out, or_5_out);
endmodule
